# Fritzing sketch Project1Wiring (saved by Fritzing 0.9.3b)
breadboards: 1

parts:
  Part1 = Arduino Nano 33 IOT  # not connected
  LED1 = LED - 5mm [color="Green (560nm)" package="5 mm [THT]"]
  LED2 = LED - 5mm [color="White (6500K)" package="5 mm [THT]"]
  LED3 = LED - 5mm [color="Red (633nm)" package="5 mm [THT]"]
  LED4 = LED - 5mm [color="White (6500K)" package="5 mm [THT]"]
  AmbientLightSensor1 = AmbientLightSensor
  DigitalTouchSensor1 = DigitalTouchSensor
  DigitalPushButtonV1 = DigitalPushButtonV2  # not connected
  R1 = Resistor [tolerance=±5% resistance=220 package="2010 [SMD]"]
  R2 = Resistor [tolerance=±5% resistance=220 package="2010 [SMD]"]
  R3 = Resistor [tolerance=±5% resistance=220 package="2010 [SMD]"]
  R4 = Resistor [tolerance=±5% resistance=220 package="2010 [SMD]"]

nets:
  N1: LED1.cathode, R3.Pin_1
  N2: LED2.cathode, R4.Pin_1
  N3: LED3.anode, R2.Pin_0
  N4: LED4.cathode, AmbientLightSensor1.VCC
  N5: LED4.anode, R1.Pin_0
  N6: AmbientLightSensor1.SIG, DigitalTouchSensor1.Signal
  GND: AmbientLightSensor1.GND, DigitalTouchSensor1.GND, R1.Pin_1, R2.Pin_1
  N7: R3.Pin_0, R4.Pin_0

notes:
  Basic breadboard wiring for Arduino
  Ground connections
  Power connections
  GND
  3v3
  Digital White LED for testing

custom parts:
  Arduino Nano 33 IOT: The Arduino Nano 33 IoT is the easiest and cheapest point of entry to enhance existing devices (and creating new ones) to be part of the IoT and designing pico-network applications. Whether you are looking at building a sensor network connected to your office or home router, or if you want to create a BLE device sending data to a cellphone, the Nano 33 IoT is your one-stop-solution for many of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
