# Fritzing sketch BreadBoardWiringProject2 (saved by Fritzing 0.9.3b)
breadboards: 1

parts:
  Part1 = Arduino Nano 33 IOT  # not connected
  R1 = Resistor [tolerance=±5% resistance=220 package="0402 [SMD]"]
  R2 = Resistor [tolerance=±5% resistance=220 package="0402 [SMD]"]
  R3 = Resistor [tolerance=±5% resistance=220 package="0402 [SMD]"]
  LED1 = LED - 5mm [color="Red (633nm)" package="5 mm [THT]"]
  LED2 = LED - 5mm [color="Green (555nm)" package="5 mm [THT]"]
  LED3 = LED - 5mm [color="White (6500K)" package="5 mm [THT]"]
  U1 = MIC [package=mic-9.7mm]
  JP1 = Header 12 [package=1x12_machine-pin-header_lock.004]
  DigitalVibrationSensor1 = DigitalVibrationSensor

nets:
  N1: R1.Pin_0, R2.Pin_0, JP1.7, DigitalVibrationSensor1.Power
  N2: R1.Pin_1, LED1.cathode
  N3: R2.Pin_1, LED2.cathode
  N4: R3.Pin_1, LED3.cathode
  N5: U1.2, JP1.11
  N6: JP1.6, DigitalVibrationSensor1.Input
  N7: JP1.8, DigitalVibrationSensor1.GND

notes:
  Basic breadboard wiring for Arduino
  Ground connections
  Power connections
  GND
  3v3

custom parts:
  Arduino Nano 33 IOT: The Arduino Nano 33 IoT is the easiest and cheapest point of entry to enhance existing devices (and creating new ones) to be part of the IoT and designing pico-network applications. Whether you are looking at building a sensor network connected to your office or home router, or if you want to create a BLE device sending data to a cellphone, the Nano 33 IoT is your one-stop-solution for many of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
